// Logisim project CPU_Final.circ as structural Verilog
module main (
  input  [4:0] in_1,
  input  in_2
);

  wire alu_1_zero, and_1_out, clock_1_out, exmem_1_zeroout, multiplexer_4_out, not_1_out, or_2_out;
  wire [1:0] control_unit_1_aluop, control_unit_1_alusrc, control_unit_1_regsrc, or_1_out;
  wire [2:0] exmem_1_wbout, idex_1_wbout, memwb_1_wbout;
  wire [2:2] control_unit_1_regwrite;
  wire [3:0] alu_control_1_control, idex_1_alucontrolout, idex_1_exout, ifid_1_instout_6;
  wire [4:0] exmem_1_mout, exmem_1_wbaddout, idex_1_wbaddout, ifid_1_instout_3, ifid_1_instout_4,
       ifid_1_instout_5, memwb_1_wbaddout;
  wire [5:0] control_unit_1_memread, idex_1_mout;
  wire [6:0] ifid_1_instout_2;
  wire [7:0] counter_1_q;
  wire [31:0] alu_1_result, exmem_1_aluout, exmem_1_pcout, exmem_1_pcpl4out, exmem_1_read2out,
       idex_1_immgenout, idex_1_pcout, idex_1_pcpl4out, idex_1_read1out, idex_1_read2out, ifid_1_pcout,
       ifid_1_pcpl4out, immgen_1_imm, memwb_1_aluout, memwb_1_pcpl4out, memwb_1_pcpliout, memwb_1_readout,
       multiplexer_1_out, multiplexer_2_out, multiplexer_3_out, multiplexer_5_out, pc2_1_pc_out, ram_1_dout,
       register_file_1_outa, register_file_1_outb, register_file_1_outregmanual, rom_1_data, somador_1_z,
       somador_2_z;
  wire [31:25] ifid_1_instout;

  Clock clock_1 (.out(clock_1_out));
  Counter counter_1 (.Q(counter_1_q), .clk(clock_1_out), .clr(in_2));  // open: load, D, count, carry, up
  PC2 pc2_1 (.clk(counter_1_q[0]), .reset(in_2), .pc_in(multiplexer_1_out), .pc_out(pc2_1_pc_out));
  ROM #(.addrWidth(24), .dataWidth(32)) rom_1 (.addr(pc2_1_pc_out[23:0]), .data(rom_1_data));
  somador somador_1 (.A(pc2_1_pc_out), .B(32'h1), .Z(somador_1_z));
  IFID ifid_1 (
    .clk(counter_1_q[0]), .pcIn(pc2_1_pc_out), .pcPl4In(somador_1_z), .instIn(rom_1_data),
    .pcOut(ifid_1_pcout), .pcPl4Out(ifid_1_pcpl4out),
    .instOut({ifid_1_instout[31], ifid_1_instout_6[3], ifid_1_instout[29:25], ifid_1_instout_4, ifid_1_instout_3, ifid_1_instout_6[2:0], ifid_1_instout_5, ifid_1_instout_2}));
  // Probe on {ifid_1_instout[31], ifid_1_instout_6[3], ifid_1_instout[29:25], ifid_1_instout_4, ifid_1_instout_3, ifid_1_instout_6[2:0], ifid_1_instout_5, ifid_1_instout_2}
  // Probe on register_file_1_outregmanual
  register_file register_file_1 (
    .\input (multiplexer_5_out), .regSelManual(in_1), .writeEnable(memwb_1_wbout[2]),
    .regASel(ifid_1_instout_3), .regBSel(ifid_1_instout_4), .writeRegSel(memwb_1_wbaddout),
    .clk(clock_1_out), .outA(register_file_1_outa), .outB(register_file_1_outb),
    .outRegManual(register_file_1_outregmanual));
  ImmGen immgen_1 (
    .inst({ifid_1_instout[31], ifid_1_instout_6[3], ifid_1_instout[29:25], ifid_1_instout_4, ifid_1_instout_3, ifid_1_instout_6[2:0], ifid_1_instout_5, ifid_1_instout_2}),
    .imm(immgen_1_imm));
  Control_Unit control_unit_1 (
    .opcode(ifid_1_instout_2), .AluSrc(control_unit_1_alusrc[0]), .blockA(control_unit_1_alusrc[1]),
    .RegWrite(control_unit_1_regwrite[2]), .MemRead(control_unit_1_memread[0]),
    .MemWrite(control_unit_1_memread[1]), .Branch(control_unit_1_memread[2]),
    .BranchNotEq(control_unit_1_memread[3]), .BrIncond(control_unit_1_memread[4]),
    .regToPC(control_unit_1_memread[5]), .AluOp(control_unit_1_aluop), .regSrc(control_unit_1_regsrc));
  Multiplexer #(.select(2), .width(32)) multiplexer_1 (
    .in0(somador_1_z), .in1(exmem_1_pcout), .in2(exmem_1_aluout), .in3(exmem_1_aluout),
    .out(multiplexer_1_out), .sel(or_1_out));
  // Probe on immgen_1_imm
  IDEX idex_1 (
    .clk(counter_1_q[0]), .pcIn(ifid_1_pcout), .read1In(register_file_1_outa),
    .read2In(register_file_1_outb), .immGenIn(immgen_1_imm), .aluControlin(ifid_1_instout_6),
    .wbAddIn(ifid_1_instout_5), .WBin({control_unit_1_regwrite[2], control_unit_1_regsrc}),
    .Min(control_unit_1_memread), .EXin({control_unit_1_aluop, control_unit_1_alusrc}),
    .pcPl4In(ifid_1_pcpl4out), .pcOut(idex_1_pcout), .read1Out(idex_1_read1out), .read2Out(idex_1_read2out),
    .immGenOut(idex_1_immgenout), .aluControlout(idex_1_alucontrolout), .wbAddOut(idex_1_wbaddout),
    .WBout(idex_1_wbout), .Mout(idex_1_mout), .EXout(idex_1_exout), .pcPl4Out(idex_1_pcpl4out));
  Multiplexer #(.width(32)) multiplexer_2 (
    .in0(idex_1_read1out), .in1({32{1'b0}}), .out(multiplexer_2_out), .sel(idex_1_exout[1]));
  Multiplexer #(.width(32)) multiplexer_3 (
    .in0(idex_1_read2out), .in1(idex_1_immgenout), .out(multiplexer_3_out), .sel(idex_1_exout[0]));
  somador somador_2 (.A(idex_1_pcout), .B(idex_1_immgenout), .Z(somador_2_z));
  ALU alu_1 (
    .A(multiplexer_2_out), .B(multiplexer_3_out), .control(alu_control_1_control), .result(alu_1_result),
    .zero(alu_1_zero));
  ALU_Control alu_control_1 (.Functs(idex_1_alucontrolout), .AluOp(idex_1_exout[3:2]), .Control(alu_control_1_control));
  EXMEM exmem_1 (
    .clk(counter_1_q[0]), .sumIn(somador_2_z), .zeroIn(alu_1_zero), .aluIn(alu_1_result),
    .read2In(idex_1_read2out), .wbAddIn(idex_1_wbaddout), .WBin(idex_1_wbout), .Min(idex_1_mout),
    .pcPl4In(idex_1_pcpl4out), .pcOut(exmem_1_pcout), .zeroOut(exmem_1_zeroout), .aluOut(exmem_1_aluout),
    .read2Out(exmem_1_read2out), .wbAddOut(exmem_1_wbaddout), .WBout(exmem_1_wbout),
    .Mout({or_1_out[1], exmem_1_mout}), .pcPl4Out(exmem_1_pcpl4out));
  or or_1 (or_1_out[0], exmem_1_mout[4], and_1_out);
  and and_1 (and_1_out, or_2_out, multiplexer_4_out);
  or or_2 (or_2_out, exmem_1_mout[2], exmem_1_mout[3]);
  Multiplexer multiplexer_4 (.in0(exmem_1_zeroout), .in1(not_1_out), .out(multiplexer_4_out), .sel(exmem_1_mout[3]));
  not not_1 (not_1_out, exmem_1_zeroout);
  RAM #(.addrWidth(24), .dataWidth(32)) ram_1 (
    .addr(exmem_1_aluout[23:0]), .we(exmem_1_mout[1]), .oe(exmem_1_mout[0]), .clk(clock_1_out),
    .din(exmem_1_read2out), .dout(ram_1_dout));
  MEMWB memwb_1 (
    .clk(counter_1_q[0]), .readIn(ram_1_dout), .aluIn(exmem_1_aluout), .wbAddIn(exmem_1_wbaddout),
    .WBin(exmem_1_wbout), .pcPl4In(exmem_1_pcpl4out), .pcPlIIn(exmem_1_pcout), .readOut(memwb_1_readout),
    .aluOut(memwb_1_aluout), .wbAddOut(memwb_1_wbaddout), .WBout(memwb_1_wbout), .pcPl4Out(memwb_1_pcpl4out),
    .pcPlIOut(memwb_1_pcpliout));
  Multiplexer #(.select(2), .width(32)) multiplexer_5 (
    .in0(memwb_1_aluout), .in1(memwb_1_readout), .in2(memwb_1_pcpl4out), .in3(memwb_1_pcpliout),
    .out(multiplexer_5_out), .sel(memwb_1_wbout[1:0]));

  // Notes on the sheet:
  //   contents of rom_1 (hex, n*v repeats v):
  //   9563
endmodule

// VHDL entity ALU, as the project stores it:
library IEEE;
use IEEE.STD_LOGIC_1164.ALL;
use ieee.numeric_std.ALL;
USE IEEE.std_logic_unsigned.ALL;

entity ALU is
    port(
    A, B       : in std_logic_vector(31 downto 0);  -- Entradas A e B de 32 bits
    control   : in std_logic_vector(3 downto 0);   -- Entrada de controle de 4 bits
    result    : out std_logic_vector(31 downto 0); -- Saída de resultado de 32 bits
    zero      : out std_logic);                    -- Saída para sinalizar se o resultado é zero
end ALU;

architecture TypeArchitecture of ALU is

signal zero_out   : std_logic_vector(32 downto 0); -- Vetor para verificação de resultado zero
signal result_out : std_logic_vector(31 downto 0); -- Vetor para armazenar o resultado da operação

begin
	
    result_out <= (A + B) when control = "0010" else                  -- Soma
    			   (A - B) when control = "0110" else                  -- Subtração
    			   (A XOR B) when control = "0101" else                -- XOR (ou exclusivo)
    			   (A OR B) when control = "0001" else                 -- OR (ou)
    			   (A AND B) when control = "0000" else                -- AND (e)
    			   (std_logic_vector(shift_left(unsigned(A), to_integer(unsigned(B))))) when control = "0011" else   -- Shift Left (deslocamento à esquerda)
    			   (std_logic_vector(shift_right(unsigned(A), to_integer(unsigned(B))))) when control = "0111";    -- Shift Right (deslocamento à direita)
        			
    result <= result_out;                          -- Atribui o valor do resultado à saída result
    zero_out(0) <= '0';                            -- Inicializa o primeiro bit de zero_out como '0'
    G2: for I in 1 to 32 generate
            zero_out(I) <= zero_out(I - 1) or result_out(I - 1);  -- Verificação de resultado zero bit a bit
    end generate;
    zero <= not zero_out(32);                      -- Sinaliza se o resultado é zero (se zero_out(32) for '0', zero é '1', caso contrário, zero é '0')
end TypeArchitecture;

// VHDL entity ALU_Control, as the project stores it:
library IEEE;
use IEEE.STD_LOGIC_1164.ALL;

entity ALU_Control is
    port(
        Functs    : IN std_logic_vector(3 downto 0);    -- Entrada de códigos de função da ALU (4 bits)
        AluOp   : IN std_logic_vector(1 downto 0);      -- Entrada de códigos de operação da ALU (2 bits)
        Control : OUT std_logic_vector(3 downto 0)      -- Saída do controle da ALU (4 bits)
        );
end ALU_Control;

architecture TypeArchitecture of ALU_Control is
begin

	control <= "0010" when AluOp = "00" else -- Se AluOp for "00", Control recebe "0010" (Operação: Soma)
			 "0110" when AluOp = "01" else -- Se AluOp for "01", Control recebe "0110" (Operação: Branch)
			 "0010" when Functs = "0000" else -- Se Functs for "0000", Control recebe "0010" (Operação: Adição)
			 "0110" when Functs = "1000" else -- Se Functs for "1000", Control recebe "0110" (Operação: Subtração)
			 "0011" when Functs = "0001" else -- Se Functs for "0001", Control recebe "0011" (Operação: Shift Left)
			 "0101" when Functs = "0100" else -- Se Functs for "0100", Control recebe "0101" (Operação: XOR)
			 "0111" when Functs = "0101" else -- Se Functs for "0101", Control recebe "0111" (Operação: Shift Right)
			 "0001" when Functs = "0110" else -- Se Functs for "0110", Control recebe "0001" (Operação: OR)
			 "0000" when Functs = "0111"; -- Se Functs for "0111", Control recebe "0000" (Operação: AND)
	 
end TypeArchitecture;

// VHDL entity Control_Unit, as the project stores it:
library IEEE;
use IEEE.STD_LOGIC_1164.ALL;

entity Control_Unit is
    port(
        opcode                     : IN  std_logic_vector(6 downto 0);  -- Entrada do código de operação (7 bits)
        AluSrc, blockA, RegWrite   : OUT std_logic;                      -- Saída de sinais de controle individuais (1 bit cada)
        MemRead, MemWrite, Branch  : OUT std_logic;                      -- Saída de sinais de controle individuais (1 bit cada)
        BranchNotEq, BrIncond      : OUT std_logic;                      -- Saída de sinais de controle individuais (1 bit cada)
        regToPC                    : OUT std_logic;                      -- Saída de sinal de controle (1 bit)
        AluOp, regSrc              : OUT std_logic_vector(1 downto 0)    -- Saída de códigos de operação da ALU e seleção de registradores (2 bits cada)
        );
end Control_Unit;

architecture TypeArchitecture of Control_Unit is
begin
    -- Processo que verifica o opcode e define os sinais de controle correspondentes
    process(opcode)
    begin
        IF (opcode = "0110011") THEN -- R-Type sem imediato (add, sub, and, or, xor, slt)
            AluSrc      <= '0';  -- Seleção de fonte para a ALU (0: A_i, 1: Immediato)
            blockA      <= '0';  -- Seleção de origem do registrador A (0: rs1, 1: zero)
            RegWrite    <= '1';  -- Habilita escrita no registrador destino
            MemRead     <= '0';  -- Habilita leitura de memória
            MemWrite    <= '0';  -- Habilita escrita na memória
            Branch      <= '0';  -- Habilita desvio condicional
            AluOp       <= "10"; -- Código de operação da ALU para R-Type (00: and, 01: or, 10: add, 11: sub)
            regSrc      <= "00"; -- Seleção de registradores para R-Type (00: rs1, 01: rs2, 10: rd, 11: zero)
            BranchNotEq <= '0';  -- Habilita desvio condicional se as entradas forem diferentes
            BrIncond    <= '0';  -- Habilita desvio incondicional
            regToPC     <= '0';  -- Seleção de registrador para atualizar o PC (0: PC+4, 1: rd)
        END IF;

        IF (opcode = "0010011") THEN -- I-Type (addi, andi, ori, xori, slti)
            AluSrc      <= '1';  -- Seleção de fonte para a ALU (0: A_i, 1: Immediato)
            blockA      <= '0';  -- Seleção de origem do registrador A (0: rs1, 1: zero)
            RegWrite    <= '1';  -- Habilita escrita no registrador destino
            MemRead     <= '0';  -- Habilita leitura de memória
            MemWrite    <= '0';  -- Habilita escrita na memória
            Branch      <= '0';  -- Habilita desvio condicional
            AluOp       <= "11"; -- Código de operação da ALU para I-Type (00: andi, 01: ori, 10: addi, 11: slti)
            regSrc      <= "00"; -- Seleção de registradores para I-Type (00: rs1, 01: rd, 10: zero)
            BranchNotEq <= '0';  -- Habilita desvio condicional se as entradas forem diferentes
            BrIncond    <= '0';  -- Habilita desvio incondicional
            regToPC     <= '0';  -- Seleção de registrador para atualizar o PC (0: PC+4, 1: rd)
        END IF;

        IF (opcode = "0100011") THEN -- S-Type (sw)
            AluSrc      <= '1';  -- Seleção de fonte para a ALU (0: A_i, 1: Immediato)
            blockA      <= '0';  -- Seleção de origem do registrador A (0: rs1, 1: zero)
            RegWrite    <= '0';  -- Habilita escrita no registrador destino
            MemRead     <= '0';  -- Habilita leitura de memória
            MemWrite    <= '1';  -- Habilita escrita na memória
            Branch      <= '0';  -- Habilita desvio condicional
            AluOp       <= "00"; -- Código de operação da ALU para S-Type (00: add)
            regSrc      <= "00"; -- Seleção de registradores para S-Type (00: rs1, 01: zero)
            BranchNotEq <= '0';  -- Habilita desvio condicional se as entradas forem diferentes
            BrIncond    <= '0';  -- Habilita desvio incondicional
            regToPC     <= '0';  -- Seleção de registrador para atualizar o PC (0: PC+4, 1: rd)
        END IF;

        IF (opcode = "1100111") THEN -- SB-Type (beq)
            AluSrc      <= '0';  -- Seleção de fonte para a ALU (0: A_i, 1: Immediato)
            blockA      <= '0';  -- Seleção de origem do registrador A (0: rs1, 1: zero)
            RegWrite    <= '0';  -- Habilita escrita no registrador destino
            MemRead     <= '0';  -- Habilita leitura de memória
            MemWrite    <= '0';  -- Habilita escrita na memória
            Branch      <= '1';  -- Habilita desvio condicional
            AluOp       <= "01"; -- Código de operação da ALU para SB-Type (01: sub)
            regSrc      <= "00"; -- Seleção de registradores para SB-Type (00: rs1, 01: rs2)
            BranchNotEq <= '0';  -- Habilita desvio condicional se as entradas forem diferentes
            BrIncond    <= '0';  -- Habilita desvio incondicional
            regToPC     <= '0';  -- Seleção de registrador para atualizar o PC (0: PC+4, 1: rd)
        END IF;

        IF (opcode = "1100011") THEN -- SB-Type (bne)
            AluSrc      <=

// VHDL entity ImmGen, as the project stores it:
library IEEE;
use IEEE.STD_LOGIC_1164.ALL;
USE IEEE.NUMERIC_STD.ALL;

entity ImmGen is
    Port( 
        inst: in std_logic_vector(31 downto 0);  -- Entrada da instrução (32 bits)
        imm: out std_logic_vector(31 downto 0)  -- Saída do valor imediato gerado (32 bits)
        );
end ImmGen;

architecture Behavioral of ImmGen is
    signal opcode       : std_logic_vector(6 downto 0);  -- Sinal para armazenar o campo opcode da instrução (7 bits)
    signal imm_interno  : std_logic_vector(31 downto 0) := "00000000000000000000000000000000";  -- Valor imediato interno inicializado com zero

begin

    opcode <= inst(6 downto 0);  -- Extrai o campo opcode da instrução

    process(opcode)
    begin
        if (opcode = "0010011" or opcode = "1100110") then  -- Tipo I (load-immediate, jump-register)
            imm_interno(11 downto 0)  <= inst(31 downto 20);  -- Extrai o imediato de 11 bits
            imm_interno(31 downto 12) <= (others => inst(31));  -- Sinal extendido para os bits mais significativos
        elsif (opcode = "1110111" or opcode = "0110111") then  -- Tipo U (lui, auipc)
            imm_interno(31 downto 12) <= inst(31 downto 12);  -- Extrai o imediato de 20 bits
        elsif (opcode = "0100011") then  -- Tipo S (store)
            imm_interno(11 downto 5)  <= inst(31 downto 25);  -- Extrai o imediato de 7 bits (5-11)
            imm_interno(4 downto 0)   <= inst(11 downto 7);   -- Extrai o imediato de 5 bits (0-4)
            imm_interno(31 downto 12) <= (others => inst(31));  -- Sinal extendido para os bits mais significativos
        elsif (opcode = "1100111" or opcode = "1100011") then  -- Tipo SB (branch)
            imm_interno(12)           <= inst(31);          -- Extrai o bit de imediato (12)
            imm_interno(11)           <= inst(7);           -- Extrai o bit de imediato (11)
            imm_interno(10 downto 5)  <= inst(30 downto 25);  -- Extrai o imediato de 6 bits (5-10)
            imm_interno(4 downto 1)   <= inst(11 downto 8);   -- Extrai o imediato de 4 bits (1-4)
            imm_interno(31 downto 13) <= (others => inst(31));  -- Sinal extendido para os bits mais significativos
        elsif (opcode = "1101111") then  -- Tipo UJ (jump)
            imm_interno(20)           <= inst(31);          -- Extrai o bit de imediato (20)
            imm_interno(19 downto 12) <= inst(19 downto 12);  -- Extrai o imediato de 8 bits (12-19)
            imm_interno(11)           <= inst(20);          -- Extrai o bit de imediato (11)
            imm_interno(10 downto 1)  <= inst(30 downto 21);  -- Extrai o imediato de 10 bits (1-10)
        end if;
    end process;

    imm <= imm_interno;  -- Define a saída como o valor imediato gerado

end Behavioral;

// VHDL entity PC2, as the project stores it:
LIBRARY ieee;
USE ieee.std_logic_1164.all;

ENTITY PC2 IS
  PORT (
  ------------------------------------------------------------------------------
  -- Inserir portas de entrada abaixo
    clk      : IN  std_logic;                    -- sinal de clock de entrada
    reset    : IN  std_logic;                    -- sinal de reset de entrada
    pc_in    : IN  std_logic_vector(31 DOWNTO 0); -- vetor de entrada exemplo
  ------------------------------------------------------------------------------
  -- Inserir portas de saída abaixo
    pc_out   : OUT std_logic_vector(31 DOWNTO 0)  -- vetor de saída exemplo
    );
END PC2;

--------------------------------------------------------------------------------
-- Descrição VHDL completa abaixo
--------------------------------------------------------------------------------

ARCHITECTURE TypeArchitecture OF PC2 IS

BEGIN

	
	PROCESS (clk, reset)
	BEGIN
		IF (rising_edge(clk)) THEN
			-- Verifica se o vetor de entrada é desconhecido (undefined) e coloca todos os bits de saída em '0'
			if (pc_in = "UUUUUUUUUUUUUUUUUUUUUUUUUUUUUUUU") then
				pc_out <= (others => '0');
			else
				pc_out <= pc_in; -- Copia o vetor de entrada para o vetor de saída
			end if;
		END IF;
		IF (reset = '1') THEN
			pc_out <= (others => '0'); -- Zera todos os bits de saída durante o reset
		END IF;
	END PROCESS;

END TypeArchitecture;

// VHDL entity somador, as the project stores it:
LIBRARY ieee;
USE ieee.std_logic_1164.all;

USE IEEE.std_logic_unsigned.ALL; -- Pacote para operações aritméticas com std_logic_vector

ENTITY somador IS
  PORT (
  ------------------------------------------------------------------------------
    A, B        : IN  std_logic_vector(31 DOWNTO 0); -- Vetor de entrada exemplo A e B de 32 bits
  ------------------------------------------------------------------------------
    Z           : OUT std_logic_vector(31 DOWNTO 0)  -- Vetor de saída exemplo Z de 32 bits
    );
END somador;

ARCHITECTURE TypeArchitecture OF somador IS

BEGIN

Z <= A + B; -- Saída Z é a soma dos vetores de entrada A e B

END TypeArchitecture;

// VHDL entity register_file, as the project stores it:
library ieee;
use ieee.std_logic_1164.all;
use ieee.numeric_std.all;

entity register_file is
  port(
    outA        : out std_logic_vector(31 downto 0);    -- Saída A do registrador
    outB        : out std_logic_vector(31 downto 0);    -- Saída B do registrador
    input       : in  std_logic_vector(31 downto 0);    -- Entrada de dado para escrita no registrador
    regSelManual: in  std_logic_vector(4 downto 0);     -- Seleção manual de um registrador de saída
    outRegManual: out std_logic_vector(31 downto 0);    -- Saída do registrador selecionado manualmente
    writeEnable : in  std_logic;                        -- Sinal de habilitação de escrita no registrador
    regASel     : in  std_logic_vector(4 downto 0);     -- Seleção do registrador A para leitura
    regBSel     : in  std_logic_vector(4 downto 0);     -- Seleção do registrador B para leitura
    writeRegSel : in  std_logic_vector(4 downto 0);     -- Seleção do registrador para escrita
    clk         : in  std_logic                        -- Sinal de clock
    );
end register_file;

architecture TypeArchitecture of register_file is
  type registerFile is array(0 to 31) of std_logic_vector(31 downto 0);
  signal registers : registerFile := 
   -- Valores iniciais dos registradores
   -- Os primeiros 32 registradores têm os valores pré-definidos como "00000000000000000000000000010000", "00000000000000000000000000000001", etc.
   -- Até o último registrador "00000000000000000000000000000000"
   ("00000000000000000000000000010000","00000000000000000000000000000001","00000000000000000000000000000000","00000000000000000000000000000000",
    "00000000000000000000000000000000","00000000000000000000000000000000","00000000000000000000000000000000","00000000000000000000000000000000",
    "00000000000000000000000000000000","00000000000000000000000000000000","00000000000000000000000000000000","00000000000000000000000000000000",
    "00000000000000000000000000000000","00000000000000000000000000000000","00000000000000000000000000000000","00000000000000000000000000000000",
    "00000000000000000000000000000000","00000000000000000000000000000000","00000000000000000000000000000000","00000000000000000000000000000000",
    "00000000000000000000000000000000","00000000000000000000000000000000","00000000000000000000000000000000","00000000000000000000000000000000",
    "00000000000000000000000000000000","00000000000000000000000000000000","00000000000000000000000000000000","00000000000000000000000000000000",
    "00000000000000000000000000000000","00000000000000000000000000000000","00000000000000000000000000000000","00000000000000000000000000000000");

begin
  regFile : process (clk) is
  begin
    if rising_edge(clk) then
      -- Read A and B before bypass
      -- Leitura dos registradores A e B antes do bypass
      if (registers(to_integer(unsigned(regASel))) = "UUUUUUUUUUUUUUUUUUUUUUUUUUUUUUUU") THEN
      	outA <= (others => '0');  -- Se o valor for "UUUU..." (indeterminado), a saída A será "0000..."
      ELSE 
      	outA <= registers(to_integer(unsigned(regASel)));  -- Caso contrário, a saída A será o valor do registrador selecionado
      END IF;
      IF (registers(to_integer(unsigned(regBSel))) = "UUUUUUUUUUUUUUUUUUUUUUUUUUUUUUUU") THEN
      	outB <= (others => '0');  -- Se o valor for "UUUU..." (indeterminado), a saída B será "0000..."
      ELSE
      	outB <= registers(to_integer(unsigned(regBSel)));  -- Caso contrário, a saída B será o valor do registrador selecionado
      END IF;
      -- Write and bypass
      -- Escrita e bypass
      if writeEnable = '1' then
        registers(to_integer(unsigned(writeRegSel))) <= input;  -- Escreve o valor da entrada no registrador selecionado
        if regASel = writeRegSel then  -- Bypass para leitura A
          outA <= input;  -- Se o registrador A é o mesmo selecionado para escrita, a saída A recebe o valor da entrada
        end if;
        if regBSel = writeRegSel then  -- Bypass para leitura B
          outB <= input;  -- Se o registrador B é o mesmo selecionado para escrita, a saída B recebe o valor da entrada
        end if;
      end if;
    end if;
  end process;

  -- seleção manual
  -- O valor de saída outRegManual recebe o valor do registrador selecionado manualmente (regSelManual)
  outRegManual <= registers(to_integer(unsigned(regSelManual)));
  
end TypeArchitecture;

// VHDL entity IFID, as the project stores it:
LIBRARY ieee;
USE ieee.std_logic_1164.all;

ENTITY IFID IS
  PORT (
    clk         : IN  std_logic;                    -- Sinal de clock
    pcIn        : IN  std_logic_vector(31 DOWNTO 0); -- Entrada do PC (contador de programa)
    pcPl4In	 : IN  std_logic_vector(31 downto 0);   -- Entrada do PC + 4 (contador de programa + 4)
    instIn      : IN  std_logic_vector(31 DOWNTO 0); -- Entrada de instrução
    pcOut       : OUT std_logic_vector(31 DOWNTO 0); -- Saída do PC (contador de programa)
    pcPl4Out	 : OUT std_logic_vector(31 downto 0);   -- Saída do PC + 4 (contador de programa + 4)
    instOut     : OUT std_logic_vector(31 DOWNTO 0)  -- Saída de instrução
    );
END IFID;

ARCHITECTURE TypeArchitecture OF IFID IS

SIGNAL IDIF : std_logic_vector(95 DOWNTO 0); -- Registrador interno (pipeline) para armazenar os dados

BEGIN

	PROCESS (clk)
	BEGIN
		IF (rising_edge(clk)) THEN
			IDIF(31 DOWNTO 0) <= instIn;        -- Armazena a instrução de entrada no registrador IDIF
			IDIF(63 DOWNTO 32) <= pcIn;         -- Armazena o valor do PC de entrada no registrador IDIF
			IDIF(95 downto 64) <= pcPl4In;      -- Armazena o valor do PC + 4 de entrada no registrador IDIF
		END IF;
		IF (falling_edge(clk)) THEN
			pcOut <= IDIF(63 DOWNTO 32);        -- Saída do valor do PC armazenado no registrador IDIF
			instOut <= IDIF(31 DOWNTO 0);       -- Saída da instrução armazenada no registrador IDIF
			pcPl4Out <= IDIF(95 downto 64);     -- Saída do valor do PC + 4 armazenado no registrador IDIF
		END IF;
	END PROCESS;

END TypeArchitecture;

// VHDL entity IDEX, as the project stores it:
LIBRARY ieee;
USE ieee.std_logic_1164.all;

ENTITY IDEX IS
  PORT (
    clk            : IN  std_logic;                    -- Sinal de clock
    pcIn           : IN  std_logic_vector(31 DOWNTO 0); -- Entrada do PC (contador de programa)
    read1In        : IN  std_logic_vector(31 DOWNTO 0); -- Entrada de leitura do registrador 1
    read2In        : IN  std_logic_vector(31 DOWNTO 0); -- Entrada de leitura do registrador 2
    immGenIn       : IN  std_logic_vector(31 DOWNTO 0); -- Entrada da unidade de geração de imediatos
    aluControlin   : IN  std_logic_vector(3 downto 0);  -- Entrada do controle da ALU (Unidade Lógica Aritmética)
    wbAddIn        : IN  std_logic_vector(4 downto 0);  -- Entrada do endereço de escrita no banco de registradores
    WBin           : IN  std_logic_vector(2 downto 0);  -- Entrada do sinal de escrita no banco de registradores
    Min            : IN  std_logic_vector(5 downto 0);  -- Entrada do sinal de escrita no banco de memória
    EXin           : IN  std_logic_vector(3 downto 0);  -- Entrada do sinal de extensão do sinal de escrita
    pcPl4In        : IN  std_logic_vector(31 downto 0); -- Entrada do PC + 4 (contador de programa + 4)

    pcOut          : OUT std_logic_vector(31 DOWNTO 0); -- Saída do PC (contador de programa)
    read1Out       : OUT std_logic_vector(31 DOWNTO 0); -- Saída de leitura do registrador 1
    read2Out       : OUT std_logic_vector(31 DOWNTO 0); -- Saída de leitura do registrador 2
    immGenOut      : OUT std_logic_vector(31 DOWNTO 0); -- Saída da unidade de geração de imediatos
    aluControlout  : OUT std_logic_vector(3 downto 0);  -- Saída do controle da ALU (Unidade Lógica Aritmética)
    wbAddOut       : OUT std_logic_vector(4 downto 0);  -- Saída do endereço de escrita no banco de registradores
    WBout          : OUT std_logic_vector(2 downto 0);  -- Saída do sinal de escrita no banco de registradores
    Mout           : OUT std_logic_vector(5 downto 0);  -- Saída do sinal de escrita no banco de memória
    EXout          : OUT std_logic_vector(3 downto 0);  -- Saída do sinal de extensão do sinal de escrita
    pcPl4Out       : OUT std_logic_vector(31 downto 0)  -- Saída do PC + 4 (contador de programa + 4)
    );
END IDEX;

ARCHITECTURE TypeArchitecture OF IDEX IS

SIGNAL idex_s : std_logic_vector(181 DOWNTO 0); -- Registrador interno (pipeline) para armazenar os dados

BEGIN

	PROCESS (clk)
	BEGIN
		IF (rising_edge(clk)) THEN
			idex_s(31 DOWNTO 0)    <= pcIn;           -- Armazena o valor do PC de entrada no registrador idex_s
			idex_s(63 DOWNTO 32)   <= read1In;        -- Armazena o valor da leitura do registrador 1 no registrador idex_s
			idex_s(95 DOWNTO 64)   <= read2In;        -- Armazena o valor da leitura do registrador 2 no registrador idex_s
			idex_s(127 DOWNTO 96)  <= immGenIn;       -- Armazena o valor da unidade de geração de imediatos no registrador idex_s
			idex_s(131 DOWNTO 128) <= aluControlin;   -- Armazena o valor do controle da ALU no registrador idex_s
			idex_s(136 DOWNTO 132) <= wbAddIn;        -- Armazena o valor do endereço de escrita no banco de registradores no registrador idex_s
			idex_s(139 downto 137) <= WBin;           -- Armazena o valor do sinal de escrita no banco de registradores no registrador idex_s
			idex_s(145 downto 140) <= Min;            -- Armazena o valor do sinal de escrita no banco de memória no registrador idex_s
			idex_s(149 downto 146) <= EXin;           -- Armazena o valor do sinal de extensão do sinal de escrita no registrador idex_s
			idex_s(181 downto 150) <= pcPl4In;        -- Armazena o valor do PC + 4 de entrada no registrador idex_s
		END IF;
		IF (falling_edge(clk)) THEN
			pcOut    <= idex_s(31 DOWNTO 0);          -- Saída do valor do PC armazenado no registrador idex_s
			read1Out  <= idex_s(63 DOWNTO 32);        -- Saída do valor da leitura do registrador 1 armazenado no registrador idex_s
			read2Out  <= idex_s(95 DOWNTO 64);        -- Saída do valor da leitura do registrador 2 armazenado no registrador idex_s
			immGenOut <= idex_s(127 DOWNTO 96);       -- Saída do valor da unidade de geração de imediatos armazenado no registrador idex_s
			aluControlout <= idex_s(131 DOWNTO 128);  -- Saída do valor do controle da ALU armazenado no registrador idex_s
			wbAddOut <= idex_s(136 DOWNTO 132);       -- Saída do valor do endereço de escrita no banco de registradores armazenado no registrador idex_s
			WBout <= idex_s(139 downto 137);          -- Saída do valor do sinal de escrita no banco de registradores armazenado no registrador idex_s
			Mout <= idex_s(145 downto 140);           -- Saída do valor do sinal de escrita no banco de memória armazenado no registrador idex_s
			EXout <= idex_s(149 downto 146);          -- Saída do valor do sinal de extensão do sinal de escrita armazenado no registrador idex_s
			pcPl4Out <= idex_s(181 downto 150);       -- Saída do valor do PC + 4 armazenado no registrador idex_s
		END IF;
	END PROCESS;
END TypeArchitecture;

// VHDL entity EXMEM, as the project stores it:
LIBRARY ieee;
USE ieee.std_logic_1164.all;

ENTITY EXMEM IS
  PORT (
    clk            : IN  std_logic;                    -- Sinal de clock
    sumIn          : IN  std_logic_vector(31 DOWNTO 0); -- Entrada do resultado da ALU
    zeroIn         : IN  std_logic;                    -- Entrada do sinal de zero da ALU
    aluIn          : IN  std_logic_vector(31 DOWNTO 0); -- Entrada do valor da ALU
    read2In        : IN  std_logic_vector(31 DOWNTO 0); -- Entrada do valor lido do registrador 2
    wbAddIn        : IN  std_logic_vector(4 downto 0);  -- Entrada do endereço de escrita no banco de registradores
    WBin           : IN  std_logic_vector(2 downto 0);  -- Entrada do sinal de escrita no banco de registradores
    Min            : IN  std_logic_vector(5 downto 0);  -- Entrada do sinal de escrita no banco de memória
    pcPl4In        : IN  std_logic_vector(31 downto 0); -- Entrada do PC + 4 (contador de programa + 4)
    
    pcOut          : OUT std_logic_vector(31 DOWNTO 0); -- Saída do valor do PC (contador de programa)
    zeroOut        : OUT std_logic;                    -- Saída do sinal de zero da ALU
    aluOut         : OUT std_logic_vector(31 DOWNTO 0); -- Saída do valor da ALU
    read2Out       : OUT std_logic_vector(31 DOWNTO 0); -- Saída do valor lido do registrador 2
    wbAddOut       : OUT std_logic_vector(4 downto 0);  -- Saída do endereço de escrita no banco de registradores
    WBout          : OUT std_logic_vector(2 downto 0);  -- Saída do sinal de escrita no banco de registradores
    Mout           : OUT std_logic_vector(5 downto 0);  -- Saída do sinal de escrita no banco de memória
    pcPl4Out       : OUT std_logic_vector(31 downto 0)  -- Saída do PC + 4 (contador de programa + 4)
    );
END EXMEM;

ARCHITECTURE TypeArchitecture OF EXMEM IS

SIGNAL exmem_s : std_logic_vector(142 DOWNTO 0); -- Registrador interno (pipeline) para armazenar os dados

BEGIN

	PROCESS (clk)
	BEGIN
		IF (rising_edge(clk)) THEN
			exmem_s(31 DOWNTO 0)   <= sumIn;          -- Armazena o valor do resultado da ALU no registrador exmem_s
			exmem_s(32)            <= zeroIn;         -- Armazena o valor do sinal de zero da ALU no registrador exmem_s
			exmem_s(64 DOWNTO 33)  <= aluIn;          -- Armazena o valor da ALU no registrador exmem_s
			exmem_s(96 DOWNTO 65)  <= read2In;        -- Armazena o valor lido do registrador 2 no registrador exmem_s
			exmem_s(101 DOWNTO 97) <= wbAddIn;        -- Armazena o valor do endereço de escrita no banco de registradores no registrador exmem_s
			exmem_s(104 DOWNTO 102) <= WBin;          -- Armazena o valor do sinal de escrita no banco de registradores no registrador exmem_s
			exmem_s(110 DOWNTO 105) <= Min;           -- Armazena o valor do sinal de escrita no banco de memória no registrador exmem_s
			exmem_s(142 downto 111) <= pcPl4In;       -- Armazena o valor do PC + 4 de entrada no registrador exmem_s
		END IF;
		IF (falling_edge(clk)) THEN
			pcOut    <=  exmem_s(31 DOWNTO 0);        -- Saída do valor do PC armazenado no registrador exmem_s
			
			if (exmem_s(32) = 'U') then               -- Verifica se o sinal de zero da ALU é desconhecido ('U')
				zeroOut <= '0';                       -- Se for desconhecido, a saída de zero é atribuída como '0'
			else
				zeroOut <= exmem_s(32);               -- Caso contrário, atribui o valor armazenado no registrador exmem_s como saída de zero
			end if; 

			if (exmem_s(64 DOWNTO 33) = "UUUUUUUUUUUUUUUUUUUUUUUUUUUUUUUU") then
				aluOut <= "00000000000000000000000000000000"; -- Se o valor da ALU for desconhecido, atribui 0 como saída da ALU
			else
				aluOut <= exmem_s(64 DOWNTO 33);       -- Caso contrário, atribui o valor armazenado no registrador exmem_s como saída da ALU
			end if;
			
			read2Out <= exmem_s(96 DOWNTO 65);       -- Saída do valor lido do registrador 2 armazenado no registrador exmem_s
			wbAddOut <= exmem_s(101 DOWNTO 97);      -- Saída do endereço de escrita no banco de registradores armazenado no registrador exmem_s
			
			if (exmem_s(109 DOWNTO 105) = "UUUUUU") then
				Mout <= "000000";                    -- Se o sinal de escrita no banco de memória for desconhecido, atribui 0 como saída do sinal de escrita no banco de memória
			else
				Mout <= exmem_s(110 DOWNTO 105);      -- Caso contrário, atribui o valor armazenado no registrador exmem_s como saída do sinal de escrita no banco de memória
			end if;
			
			WBout <= exmem_s(104 DOWNTO 102);        -- Saída do sinal de escrita no banco de registradores armazenado no registrador exmem_s

			pcPl4Out <= exmem_s(142 downto 111);     -- Saída do valor do PC + 4 armazenado no registrador exmem_s
		END IF;
	END PROCESS;
END TypeArchitecture;

// VHDL entity MEMWB, as the project stores it:
LIBRARY ieee;
USE ieee.std_logic_1164.all;

ENTITY MEMWB IS
  PORT (
    clk            : IN  std_logic;                     -- Sinal de clock
    readIn         : IN  std_logic_vector(31 DOWNTO 0); -- Entrada do valor lido da memória
    aluIn          : IN  std_logic_vector(31 DOWNTO 0); -- Entrada do valor da ALU
    wbAddIn        : IN  std_logic_vector(4 downto 0);  -- Entrada do endereço de escrita no banco de registradores
    WBin           : IN  std_logic_vector(2 downto 0);  -- Entrada do sinal de escrita no banco de registradores
    pcPl4In        : IN  std_logic_vector(31 downto 0); -- Entrada do PC + 4 (contador de programa + 4) vindo do estágio MEM
    pcPlIIn        : IN  std_logic_vector(31 downto 0); -- Entrada do PC + I (próxima instrução) vindo do estágio MEM
    
    readOut        : OUT std_logic_vector(31 DOWNTO 0); -- Saída do valor lido da memória
    aluOut         : OUT std_logic_vector(31 DOWNTO 0); -- Saída do valor da ALU
    wbAddOut       : OUT std_logic_vector(4 downto 0);  -- Saída do endereço de escrita no banco de registradores
    WBout          : OUT std_logic_vector(2 downto 0);  -- Saída do sinal de escrita no banco de registradores
    pcPl4Out       : OUT std_logic_vector(31 downto 0); -- Saída do PC + 4 (contador de programa + 4) para o estágio WB
    pcPlIOut       : OUT std_logic_vector(31 downto 0)  -- Saída do PC + I (próxima instrução) para o estágio IF
    );
END MEMWB;

ARCHITECTURE TypeArchitecture OF MEMWB IS

SIGNAL memwb_s : std_logic_vector(135 DOWNTO 0); -- Registrador interno (pipeline) para armazenar os dados

BEGIN

	PROCESS (clk)
	BEGIN
		IF (rising_edge(clk)) THEN
			memwb_s(31 DOWNTO 0)   <= readIn;          -- Armazena o valor lido da memória no registrador memwb_s
			memwb_s(63 DOWNTO 32)  <= aluIn;           -- Armazena o valor da ALU no registrador memwb_s
			memwb_s(68 DOWNTO 64)  <= wbAddIn;         -- Armazena o endereço de escrita no banco de registradores no registrador memwb_s
			memwb_s(71 DOWNTO 69)  <= WBin;            -- Armazena o sinal de escrita no banco de registradores no registrador memwb_s
			memwb_s(103 downto 72) <= pcPl4In;         -- Armazena o valor do PC + 4 vindo do estágio MEM no registrador memwb_s
			memwb_s(135 downto 104) <= pcPlIIn;        -- Armazena o valor do PC + I vindo do estágio MEM no registrador memwb_s
			
		END IF;
		IF (falling_edge(clk)) THEN
			readOut    <=  memwb_s(31 DOWNTO 0);       -- Saída do valor lido da memória armazenado no registrador memwb_s
			aluOut  <=  memwb_s(63 DOWNTO 32);         -- Saída do valor da ALU armazenado no registrador memwb_s
			wbAddOut <= memwb_s(68 DOWNTO 64);         -- Saída do endereço de escrita no banco de registradores armazenado no registrador memwb_s
			WBout <= memwb_s(71 DOWNTO 69);            -- Saída do sinal de escrita no banco de registradores armazenado no registrador memwb_s
			pcPl4Out <= memwb_s(103 downto 72);        -- Saída do valor do PC + 4 armazenado no registrador memwb_s
			pcPlIOut <= memwb_s(135 downto 104);       -- Saída do valor do PC + I armazenado no registrador memwb_s
		END IF;
	END PROCESS;
END TypeArchitecture;
