// Logisim project CPU_Vetorial.circ as structural Verilog
module main (
  input  [4:0] in_1,
  input  in_2
);

  wire alu_1_zero, and_1_out, clock_1_out, d_ff_1_q, exmem_1_zeroout, multiplexer_5_out, not_1_out, or_2_out;
  wire [1:0] control_unit_1_aluop, control_unit_1_regsrc, control_unit_1_vecsize, or_1_out;
  wire [2:0] exmem_1_wbout, idex_1_wbout, memwb_1_wbout;
  wire [2:2] control_unit_1_regwrite;
  wire [3:0] alu_control_1_control, idex_1_alucontrolout, ifid_1_instout_6;
  wire [4:0] control_unit_1_alusrc, exmem_1_mout, exmem_1_wbaddout, idex_1_wbaddout, ifid_1_instout_3,
       ifid_1_instout_4, ifid_1_instout_5, memwb_1_wbaddout;
  wire [5:0] control_unit_1_memread, idex_1_mout;
  wire [6:0] idex_1_exout, ifid_1_instout_2;
  wire [7:0] counter_1_q;
  wire [31:0] alu_1_result, exmem_1_aluout, exmem_1_pcout, exmem_1_pcpl4out, exmem_1_read2out,
       idex_1_immgenout, idex_1_pcout, idex_1_pcpl4out, idex_1_read1out, idex_1_read2out, ifid_1_pcout,
       ifid_1_pcpl4out, immgen_1_imm, memwb_1_aluout, memwb_1_pcpl4out, memwb_1_pcpliout, memwb_1_readout,
       multiplexer_1_out, multiplexer_2_out, multiplexer_3_out, multiplexer_4_out, multiplexer_6_out,
       pc2_1_pc_out, ram_1_dout, register_file_1_outa, register_file_1_outb, register_file_1_outregmanual,
       rom_1_data, somador_1_z, somador_2_z;
  wire [31:25] ifid_1_instout;

  Clock clock_1 (.out(clock_1_out));
  Multiplexer #(.width(32)) multiplexer_1 (
    .in0(multiplexer_2_out), .in1(somador_1_z), .out(multiplexer_1_out), .sel(d_ff_1_q));
  D_Flip_Flop d_ff_1 (.D(1'b0), .clk(clock_1_out), .Q(d_ff_1_q));  // open: Qn, preset, reset
  Counter counter_1 (.Q(counter_1_q), .clk(clock_1_out), .clr(in_2));  // open: load, D, count, carry, up
  PC2 pc2_1 (.clk(counter_1_q[0]), .reset(in_2), .pc_in(multiplexer_1_out), .pc_out(pc2_1_pc_out));
  ROM #(.addrWidth(24), .dataWidth(32)) rom_1 (.addr(pc2_1_pc_out[23:0]), .data(rom_1_data));
  somador somador_1 (.A(pc2_1_pc_out), .B(32'h1), .Z(somador_1_z));
  IFID ifid_1 (
    .clk(counter_1_q[0]), .pcIn(pc2_1_pc_out), .pcPl4In(somador_1_z), .instIn(rom_1_data),
    .pcOut(ifid_1_pcout), .pcPl4Out(ifid_1_pcpl4out),
    .instOut({ifid_1_instout[31], ifid_1_instout_6[3], ifid_1_instout[29:25], ifid_1_instout_4, ifid_1_instout_3, ifid_1_instout_6[2:0], ifid_1_instout_5, ifid_1_instout_2}));
  // Probe on {ifid_1_instout[31], ifid_1_instout_6[3], ifid_1_instout[29:25], ifid_1_instout_4, ifid_1_instout_3, ifid_1_instout_6[2:0], ifid_1_instout_5, ifid_1_instout_2}
  // Probe on register_file_1_outregmanual
  register_file register_file_1 (
    .\input (multiplexer_6_out), .regSelManual(in_1), .writeEnable(memwb_1_wbout[2]),
    .regASel(ifid_1_instout_3), .regBSel(ifid_1_instout_4), .writeRegSel(memwb_1_wbaddout),
    .clk(clock_1_out), .outA(register_file_1_outa), .outB(register_file_1_outb),
    .outRegManual(register_file_1_outregmanual));
  ImmGen immgen_1 (
    .inst({ifid_1_instout[31], ifid_1_instout_6[3], ifid_1_instout[29:25], ifid_1_instout_4, ifid_1_instout_3, ifid_1_instout_6[2:0], ifid_1_instout_5, ifid_1_instout_2}),
    .imm(immgen_1_imm));
  Control_Unit control_unit_1 (
    .opcode(ifid_1_instout_2), .AluSrc(control_unit_1_alusrc[0]), .blockA(control_unit_1_alusrc[1]),
    .RegWrite(control_unit_1_regwrite[2]), .MemRead(control_unit_1_memread[0]),
    .MemWrite(control_unit_1_memread[1]), .Branch(control_unit_1_memread[2]),
    .BranchNotEq(control_unit_1_memread[3]), .BrIncond(control_unit_1_memread[4]),
    .regToPC(control_unit_1_memread[5]), .mode(control_unit_1_alusrc[4]), .AluOp(control_unit_1_aluop),
    .regSrc(control_unit_1_regsrc), .vecSize(control_unit_1_vecsize));
  Multiplexer #(.select(2), .width(32)) multiplexer_2 (
    .in0(somador_1_z), .in1(exmem_1_pcout), .in2(exmem_1_aluout), .in3(exmem_1_aluout),
    .out(multiplexer_2_out), .sel(or_1_out));
  // Probe on immgen_1_imm
  IDEX idex_1 (
    .clk(counter_1_q[0]), .pcIn(ifid_1_pcout), .read1In(register_file_1_outa),
    .read2In(register_file_1_outb), .immGenIn(immgen_1_imm), .aluControlin(ifid_1_instout_6),
    .wbAddIn(ifid_1_instout_5), .WBin({control_unit_1_regwrite[2], control_unit_1_regsrc}),
    .Min(control_unit_1_memread),
    .EXin({control_unit_1_vecsize, control_unit_1_alusrc[4], control_unit_1_aluop, control_unit_1_alusrc[1:0]}),
    .pcPl4In(ifid_1_pcpl4out), .pcOut(idex_1_pcout), .read1Out(idex_1_read1out), .read2Out(idex_1_read2out),
    .immGenOut(idex_1_immgenout), .aluControlout(idex_1_alucontrolout), .wbAddOut(idex_1_wbaddout),
    .WBout(idex_1_wbout), .Mout(idex_1_mout), .EXout(idex_1_exout), .pcPl4Out(idex_1_pcpl4out));
  Multiplexer #(.width(32)) multiplexer_3 (
    .in0(idex_1_read1out), .in1({32{1'b0}}), .out(multiplexer_3_out), .sel(idex_1_exout[1]));
  Multiplexer #(.width(32)) multiplexer_4 (
    .in0(idex_1_read2out), .in1(idex_1_immgenout), .out(multiplexer_4_out), .sel(idex_1_exout[0]));
  somador somador_2 (.A(idex_1_pcout), .B(idex_1_immgenout), .Z(somador_2_z));
  ALU alu_1 (
    .A(multiplexer_3_out), .B(multiplexer_4_out), .control(alu_control_1_control), .mode(idex_1_exout[4]),
    .vecSize(idex_1_exout[6:5]), .result(alu_1_result), .zero(alu_1_zero));
  ALU_Control alu_control_1 (.Functs(idex_1_alucontrolout), .AluOp(idex_1_exout[3:2]), .Control(alu_control_1_control));
  EXMEM exmem_1 (
    .clk(counter_1_q[0]), .sumIn(somador_2_z), .zeroIn(alu_1_zero), .aluIn(alu_1_result),
    .read2In(idex_1_read2out), .wbAddIn(idex_1_wbaddout), .WBin(idex_1_wbout), .Min(idex_1_mout),
    .pcPl4In(idex_1_pcpl4out), .pcOut(exmem_1_pcout), .zeroOut(exmem_1_zeroout), .aluOut(exmem_1_aluout),
    .read2Out(exmem_1_read2out), .wbAddOut(exmem_1_wbaddout), .WBout(exmem_1_wbout),
    .Mout({or_1_out[1], exmem_1_mout}), .pcPl4Out(exmem_1_pcpl4out));
  or or_1 (or_1_out[0], exmem_1_mout[4], and_1_out);
  and and_1 (and_1_out, or_2_out, multiplexer_5_out);
  or or_2 (or_2_out, exmem_1_mout[2], exmem_1_mout[3]);
  Multiplexer multiplexer_5 (.in0(exmem_1_zeroout), .in1(not_1_out), .out(multiplexer_5_out), .sel(exmem_1_mout[3]));
  not not_1 (not_1_out, exmem_1_zeroout);
  RAM #(.addrWidth(24), .dataWidth(32)) ram_1 (
    .addr(exmem_1_aluout[23:0]), .we(exmem_1_mout[1]), .oe(exmem_1_mout[0]), .clk(clock_1_out),
    .din(exmem_1_read2out), .dout(ram_1_dout));
  MEMWB memwb_1 (
    .clk(counter_1_q[0]), .readIn(ram_1_dout), .aluIn(exmem_1_aluout), .wbAddIn(exmem_1_wbaddout),
    .WBin(exmem_1_wbout), .pcPl4In(exmem_1_pcpl4out), .pcPlIIn(exmem_1_pcout), .readOut(memwb_1_readout),
    .aluOut(memwb_1_aluout), .wbAddOut(memwb_1_wbaddout), .WBout(memwb_1_wbout), .pcPl4Out(memwb_1_pcpl4out),
    .pcPlIOut(memwb_1_pcpliout));
  Multiplexer #(.select(2), .width(32)) multiplexer_6 (
    .in0(memwb_1_aluout), .in1(memwb_1_readout), .in2(memwb_1_pcpl4out), .in3(memwb_1_pcpliout),
    .out(multiplexer_6_out), .sel(memwb_1_wbout[1:0]));

  // Notes on the sheet:
  //   contents of rom_1 (hex, n*v repeats v):
  //   100180
endmodule

// VHDL entity ALU, as the project stores it:
library IEEE;
use IEEE.STD_LOGIC_1164.ALL;
use ieee.numeric_std.ALL;
USE IEEE.std_logic_unsigned.ALL;

entity ALU is
    port(
    A, B       : in std_logic_vector(31 downto 0);   -- Entradas A e B de 32 bits
    control   : in std_logic_vector(3 downto 0);    -- Sinal de controle de 4 bits para selecionar a operação
    mode      : in std_logic;                       -- Modo de operação: 0 para operação única e 1 para operação vetorial
    vecSize   : in std_logic_vector(1 downto 0);    -- Tamanho do vetor de operações (usado no modo vetorial)
    result    : out std_logic_vector(31 downto 0);  -- Saída da operação única (modo 0)
    zero      : out std_logic                       -- Sinal de saída indicando se o resultado é zero
    );
end ALU;

architecture TypeArchitecture of ALU is

-- Declaração dos sinais internos da ALU
signal zero_out   : std_logic_vector(32 downto 0);
signal zero_vec   : std_logic_vector(32 downto 0);
signal result_out : std_logic_vector(31 downto 0);
signal result_vec : std_logic_vector(31 downto 0);
signal add_vec    : std_logic_vector(31 downto 0);
signal sub_vec    : std_logic_vector(31 downto 0);
signal shiftl_vec : std_logic_vector(31 downto 0);
signal shiftr_vec : std_logic_vector(31 downto 0);

signal A3116 	   : std_logic_vector(15 downto 0);
signal A1500 	   : std_logic_vector(15 downto 0);

signal A3124      : std_logic_vector(7 downto 0);
signal A2316      : std_logic_vector(7 downto 0);
signal A1508      : std_logic_vector(7 downto 0);
signal A0700      : std_logic_vector(7 downto 0);

signal A3128      : std_logic_vector(3 downto 0);
signal A2724      : std_logic_vector(3 downto 0);
signal A2320      : std_logic_vector(3 downto 0);
signal A1916      : std_logic_vector(3 downto 0);
signal A1512      : std_logic_vector(3 downto 0);
signal A1108      : std_logic_vector(3 downto 0);
signal A0704      : std_logic_vector(3 downto 0);
signal A0300      : std_logic_vector(3 downto 0);

signal intB       : integer;

begin

	-- Conversão da entrada B para inteiro para uso nas operações de deslocamento
	intB <= to_integer(unsigned(B));

	-- Divisão do sinal de entrada A para partes menores para cálculos vetoriais
	A3116 <= A(31 downto 16);
	A1500 <= A(15 downto 0);

	A3124 <= A(31 downto 24);
	A2316 <= A(23 downto 16);
	A1508 <= A(15 downto 8);
	A0700 <= A(7 downto 0);

	A3128 <= A(31 downto 28);
	A2724 <= A(27 downto 24);
	A2320 <= A(23 downto 20);
	A1916 <= A(19 downto 16);
	A1512 <= A(15 downto 12);
	A1108 <= A(11 downto 8);
	A0704 <= A(7 downto 4);
	A0300 <= A(3 downto 0);
	
	-- Cálculos das operações vetoriais com base no tamanho do vetor (vecSize)
	add_vec <= (A + B) when vecSize = "11" else
			 ((A3116 + B(31 downto 16)) & (A1500 + B(15 downto 0))) when vecSize = "10" else
			 ((A3124 + B(31 downto 24)) & (A2316 + B(23 downto 16)) & (A1508 + B(15 downto 8)) & (A0700 + B(7 downto 0))) when vecSize = "01" else
			 ((A3128 + B(31 downto 28)) & (A2724 + B(27 downto 24)) & (A2320 + B(23 downto 20)) & (A1916 + B(19 downto 16)) & (A1512 + B(15 downto 12)) & (A1108 + B(11 downto 8)) & (A0704 + B(7 downto 4)) & (A0300 + B(3 downto 0))) when vecSize = "00";
	
	sub_vec <= (A - B) when vecSize = "11" else
			 ((A3116 - B(31 downto 16)) & (A1500 - B(15 downto 0))) when vecSize = "10" else
			 ((A3124 - B(31 downto 24)) & (A2316 - B(23 downto 16)) & (A1508 - B(15 downto 8)) & (A0700 - B(7 downto 0))) when vecSize = "01" else
			 ((A3128 - B(31 downto 28)) & (A2724 - B(27 downto 24)) & (A2320 - B(23 downto 20)) & (A1916 - B(19 downto 16)) & (A1512 - B(15 downto 12)) & (A1108 - B(11 downto 8)) & (A0704 - B(7 downto 4)) & (A0300 - B(3 downto 0))) when vecSize = "00";
	
	-- Cálculos das operações de deslocamento vetoriais
	shiftl_vec <= (std_logic_vector(shift_left(unsigned(A), intB))) when vecSize = "11" else
			 ((std_logic_vector(shift_left(unsigned(A3116), intB))) & std_logic_vector(shift_left(unsigned(A1500), intB))) when vecSize = "10" else
			 ((std_logic_vector(shift_left(unsigned(A3124), intB))) & (std_logic_vector(shift_left(unsigned(A2316), intB))) & (std_logic_vector(shift_left(unsigned(A1508), intB))) & (std_logic_vector(shift_left(unsigned(A0700), intB)))) when vecSize = "01" else
			 ((std_logic_vector(shift_left(unsigned(A3128), intB))) & (std_logic_vector(shift_left(unsigned(A2724), intB))) & (std_logic_vector(shift_left(unsigned(A2320), intB))) & (std_logic_vector(shift_left(unsigned(A1916), intB))) & (std_logic_vector(shift_left(unsigned(A1512), intB))) & (std_logic_vector(shift_left(unsigned(A1108), intB))) & (std_logic_vector(shift_left(unsigned(A0704), intB))) & (std_logic_vector(shift_left(unsigned(A0300), intB)))) when vecSize = "00";

	shiftr_vec <= (std_logic_vector(shift_right(unsigned(A), intB))) when vecSize = "11" else
			 ((std_logic_vector(shift_right(unsigned(A3116), intB))) & std_logic_vector(shift_right(unsigned(A1500), intB))) when vecSize = "10" else
			 ((std_logic_vector(shift_right(unsigned(A3124), intB))) & (std_logic_vector(shift_right(unsigned(A2316), intB))) & (std_logic_vector(shift_right(unsigned(A1508), intB))) & (std_logic_vector(shift_right(unsigned(A0700), intB)))) when vecSize = "01" else
			 ((std_logic_vector(shift_right(unsigned(A3128), intB))) & (std_logic_vector(shift_right(unsigned(A2724), intB))) & (std_logic_vector(shift_right(unsigned(A2320), intB))) & (std_logic_vector(shift_right(unsigned(A1916), intB))) & (std_logic_vector(shift_right(unsigned(A1512), intB))) & (std_logic_vector(shift_right(unsigned(A1108), intB))) & (std_logic_vector(shift_right(unsigned(A0704), intB))) & (std_logic_vector(shift_right(unsigned(A0300), intB)))) when vecSize = "00";
	
	-- Seleção da operação de acordo com o sinal de controle (control)
	result_vec <= add_vec when control = "0010" else
			    sub_vec when control = "0110" else
			    shiftl_vec when control = "0011" else
			    shiftr_vec when control = "0111" else
			    (others => '0');

	-- Seleção da operação no modo único ou vetorial (modo 0 ou 1)
    result_out <= (A + B) when control = "0010" else
    			   (A - B) when control = "0110" else
    			   (A XOR B) when control = "0101" else
    			   (A OR B) when control = "0001" else
    			   (A AND B) when control = "0000" else
    			   (std_logic_vector(shift_left(unsigned(A), intB))) when control = "0011" else
    			   (std_logic_vector(shift_right(unsigned(A), intB))) when control = "0111";
        			
    result <= result_out when mode = '0' else
    		    result_vec when mode = '1';
    		    
    -- Cálculo dos sinais de saída zero para modo único e vetorial
    zero_out(0)<= '0';
    zero_vec(0) <= '0';
    G2: for I in 1 to 32 generate
            zero_out(I) <= zero_out(I - 1) or result_out(I - 1);
            zero_vec(I) <= zero_vec(I - 1) or result_vec(I - 1);
    end generate;
    zero <= (not zero_out(32)) when mode = '0' else
    		  (not zero_vec(32)) when mode = '1';
end TypeArchitecture;

// VHDL entity ALU_Control, as the project stores it:
library IEEE;
use IEEE.STD_LOGIC_1164.ALL;

entity ALU_Control is
    port(
        Functs    : IN std_logic_vector(3 downto 0);   -- Entrada que contém o código da função da ALU
        AluOp     : IN std_logic_vector(1 downto 0);   -- Entrada que contém o código da operação da ALU
        Control   : OUT std_logic_vector(3 downto 0)   -- Saída que contém o sinal de controle da ALU
        );
end ALU_Control;

architecture TypeArchitecture of ALU_Control is
begin

	-- Lógica para gerar o sinal de controle (Control) com base nas entradas Functs e AluOp
	control <= "0010" when AluOp = "00" else   -- Operação de adição
			 "0110" when AluOp = "01" else   -- Operação de subtração
			 "0010" when Functs = "0000" else -- Funct = 0000, operação de adição
			 "0110" when Functs = "1000" else -- Funct = 1000, operação de subtração
			 "0011" when Functs = "0001" else -- Funct = 0001, operação de shift left
			 "0101" when Functs = "0100" else -- Funct = 0100, operação de XOR
			 "0111" when Functs = "0101" else -- Funct = 0101, operação de shift right
			 "0001" when Functs = "0110" else -- Funct = 0110, operação de OR
			 "0000" when Functs = "0111";     -- Funct = 0111, operação de AND
			 
	-- As combinações restantes de Functs e AluOp não têm uma operação específica definida.
	-- Caso nenhuma das condições acima seja satisfeita, o sinal de controle será "0000" (AND).
	
end TypeArchitecture;

// VHDL entity Control_Unit, as the project stores it:
library IEEE;
use IEEE.STD_LOGIC_1164.ALL;

entity Control_Unit is
    port(
        opcode                     : IN  std_logic_vector(6 downto 0); -- Entrada que contém o opcode da instrução
        AluSrc, blockA, RegWrite 	: OUT std_logic;                   -- Sinais de controle da ALU
        MemRead, MemWrite, Branch  : OUT std_logic;                   -- Sinais de controle de memória
        BranchNotEq, BrIncond		: OUT std_logic;                   -- Sinais de controle para desvios condicionais e incondicionais
        regToPC, mode			    : OUT std_logic;                   -- Sinais de controle para modificação do PC (Contador de Programa)
        AluOp,regSrc, vecSize		: OUT std_logic_vector(1 downto 0) -- Sinais de controle adicionais para a ALU
        );
end Control_Unit;

architecture TypeArchitecture of Control_Unit is

begin
	process(opcode)
	begin
	    -- Bloco de seleção para gerar os sinais de controle com base no opcode da instrução
	    IF (opcode = "0110011") THEN -- R-Type sem imediato
	        AluSrc      <= '0';
	        blockA      <= '0';
	        RegWrite    <= '1';
	        MemRead     <= '0';
	        MemWrite    <= '0';
	        Branch      <= '0';
	        AluOp       <= "10";
	        regSrc      <= "00";
	        BranchNotEq <= '0';
	        BrIncond    <= '0';
	        regToPC     <= '0';
	        mode        <= '0';     
	        vecSize     <= "00";
	    END IF;
	    
	    -- Mais blocos IF/THEN/ELSE para mapear os demais opcodes às operações e sinais de controle correspondentes.
	    -- Cada bloco IF/THEN/ELSE representa uma instrução diferente, definindo quais sinais de controle devem ser ativados
	    -- para cada tipo de instrução.

	end process;
end TypeArchitecture;

// VHDL entity ImmGen, as the project stores it:
library IEEE;
use IEEE.STD_LOGIC_1164.ALL;
USE IEEE.NUMERIC_STD.ALL;

entity ImmGen is
    Port( 
        inst: in std_logic_vector(31 downto 0); -- Entrada contendo a instrução de 32 bits
        imm: out std_logic_vector(31 downto 0)  -- Saída contendo o imediato de 32 bits
    );
end ImmGen;

architecture Behavioral of ImmGen is
    -- Declaração de sinais para armazenar o opcode e o imediato interno.
    signal opcode        : std_logic_vector(6 downto 0); 
    signal imm_interno   : std_logic_vector(31 downto 0) := "00000000000000000000000000000000"; -- Inicializa o imediato interno com valor '0'.

begin
    -- Extrai o opcode da instrução de entrada.
    opcode <= inst(6 downto 0);

    process(opcode)
    begin
        -- Bloco de seleção para gerar o imediato com base no opcode da instrução
        if (opcode = "0010011" or opcode = "1100110" or opcode = "0000100" or opcode = "0000101" or opcode = "0000001") then --I type
            imm_interno(11 downto 0)  <= inst(31 downto 20);     -- Bits 31:20 são copiados diretamente para os bits 11:0 do imediato
            imm_interno(31 downto 12) <= (others => inst(31));  -- O bit 31 é copiado para todos os bits 31:12 do imediato
        elsif (opcode = "1110111" or opcode = "0110111" or opcode = "0001000" or opcode = "0001001" or opcode = "0001010") then -- U type
            imm_interno(31 downto 12) <= inst(31 downto 12);    -- Bits 31:12 são copiados diretamente para os bits 31:12 do imediato
        elsif (opcode = "0100011") then -- S type
            imm_interno(11 downto 5) <= inst(31 downto 25);     -- Bits 31:25 são copiados diretamente para os bits 11:5 do imediato
            imm_interno(4 downto 0)  <= inst(11 downto 7);      -- Bits 11:7 são copiados diretamente para os bits 4:0 do imediato
            imm_interno(31 downto 12) <= (others => inst(31));  -- O bit 31 é copiado para todos os bits 31:12 do imediato
        elsif (opcode = "1100111" or opcode = "1100011") then -- SB type
            imm_interno(12) <= inst(31);                       -- O bit 31 é copiado para o bit 12 do imediato
            imm_interno(11) <= inst(7);                        -- O bit 7 é copiado para o bit 11 do imediato
            imm_interno(10 downto 5) <= inst(30 downto 25);     -- Bits 30:25 são copiados diretamente para os bits 10:5 do imediato
            imm_interno(4 downto 1) <= inst(11 downto 8);       -- Bits 11:8 são copiados diretamente para os bits 4:1 do imediato
            imm_interno(31 downto 13) <= (others => inst(31));  -- O bit 31 é copiado para todos os bits 31:13 do imediato
        elsif (opcode = "1101111") then -- UJ type
            imm_interno(20) <= inst(31);                       -- O bit 31 é copiado para o bit 20 do imediato
            imm_interno(19 downto 12) <= inst(19 downto 12);    -- Bits 19:12 são copiados diretamente para os bits 19:12 do imediato
            imm_interno(11) <= inst(20);                       -- O bit 20 é copiado para o bit 11 do imediato
            imm_interno(10 downto 1) <= inst(30 downto 21);     -- Bits 30:21 são copiados diretamente para os bits 10:1 do imediato
        end if;
    end process;

    -- Saída do imediato gerado.
    imm <= imm_interno;

end Behavioral;

// VHDL entity PC2, as the project stores it:
LIBRARY ieee;
USE ieee.std_logic_1164.all;

ENTITY PC2 IS
  PORT (
    -- Portas de entrada
    clk      : IN  std_logic;                    -- Sinal de clock (entrada)
    reset    : IN  std_logic;                    -- Sinal de reset (entrada)
    pc_in    : IN  std_logic_vector(31 DOWNTO 0); -- Dado de entrada de 32 bits (vetor de entrada)
    
    -- Portas de saída
    pc_out   : OUT std_logic_vector(31 DOWNTO 0)  -- Dado de saída de 32 bits (vetor de saída)
  );
END PC2;

ARCHITECTURE TypeArchitecture OF PC2 IS
BEGIN
	PROCESS (clk, reset)
	BEGIN
		IF (rising_edge(clk)) THEN
			if (pc_in = "UUUUUUUUUUUUUUUUUUUUUUUUUUUUUUUU") then
				-- Se a entrada for desconhecida (U), o dado de saída é zerado.
				pc_out <= (others => '0');
			else
				-- Caso contrário, copia o dado de entrada para a saída.
				pc_out <= pc_in;
			end if;
		END IF;
		IF (reset = '1') THEN
			-- Se o sinal de reset for '1', o dado de saída é zerado.
			pc_out <= (others => '0');
		END IF;
	END PROCESS;
END TypeArchitecture;

// VHDL entity somador, as the project stores it:
LIBRARY ieee;
USE ieee.std_logic_1164.all;
USE IEEE.std_logic_unsigned.ALL;

ENTITY somador IS
  PORT (
    -- Portas de entrada
    A, B        : IN  std_logic_vector(31 DOWNTO 0); -- Números de entrada de 32 bits (vetor de entrada)
    
    -- Porta de saída
    Z           : OUT std_logic_vector(31 DOWNTO 0)  -- Resultado da soma (vetor de saída)
  );
END somador;

ARCHITECTURE TypeArchitecture OF somador IS
BEGIN

  -- O sinal de saída Z recebe a soma dos valores de A e B.
  Z <= A + B;

END TypeArchitecture;

// VHDL entity register_file, as the project stores it:
library ieee;
use ieee.std_logic_1164.all;
use ieee.numeric_std.all;

entity register_file is
  port(
    -- Portas de saída
    outA        : out std_logic_vector(31 downto 0);  -- Saída do registro A
    outB        : out std_logic_vector(31 downto 0);  -- Saída do registro B
    outRegManual: out std_logic_vector(31 downto 0);  -- Saída de um registro selecionado manualmente
    
    -- Portas de entrada
    input       : in  std_logic_vector(31 downto 0);  -- Dado de entrada para escrever em um registro
    regSelManual: in  std_logic_vector(4 downto 0);   -- Seleção manual de registro de saída
    writeEnable : in  std_logic;                     -- Sinal de habilitação de escrita em um registro
    regASel     : in  std_logic_vector(4 downto 0);   -- Seleção do registrador A para leitura
    regBSel     : in  std_logic_vector(4 downto 0);   -- Seleção do registrador B para leitura
    writeRegSel : in  std_logic_vector(4 downto 0);   -- Seleção do registrador para escrita
    clk         : in  std_logic                      -- Sinal de clock
    );
end register_file;

architecture TypeArchitecture of register_file is
  -- Declaração de um tipo array que representa o banco de registradores com 32 registros de 32 bits cada
  type registerFile is array(0 to 31) of std_logic_vector(31 downto 0);
  -- Declaração de um sinal (variável interna) chamado "registers" do tipo registerFile
  signal registers : registerFile := 
   ("00000000000000000000000000011111","00000000000000000000000000000001","00000000000000000000000000000000","00000000000000000000000000000000",
    "00000000000000000000000000000000","00000000000000000000000000000000","00000000000000000000000000000000","00000000000000000000000000000000",
    "00000000000000000000000000000000","00000000000000000000000000000000","00000000000000000000000000000000","00000000000000000000000000000000",
    "00000000000000000000000000000000","00000000000000000000000000000000","00000000000000000000000000000000","00000000000000000000000000000000",
    "00000000000000000000000000000000","00000000000000000000000000000000","00000000000000000000000000000000","00000000000000000000000000000000",
    "00000000000000000000000000000000","00000000000000000000000000000000","00000000000000000000000000000000","00000000000000000000000000000000",
    "00000000000000000000000000000000","00000000000000000000000000000000","00000000000000000000000000000000","00000000000000000000000000000000",
    "00000000000000000000000000000000","00000000000000000000000000000000","00000000000000000000000000000000","00000000000000000000000000000000");
begin
  regFile : process (clk) is
  begin
    if rising_edge(clk) then
      -- Read A and B before bypass
      -- Realiza a leitura dos registradores A e B antes de fazer o bypass
      if (registers(to_integer(unsigned(regASel))) = "UUUUUUUUUUUUUUUUUUUUUUUUUUUUUUUU") THEN
        outA <= (others => '0');  -- Se o registro for inválido (contém "U"), a saída é zerada
      else 
        outA <= registers(to_integer(unsigned(regASel)));  -- Caso contrário, a saída é o valor do registrador A
      end if;
      IF (registers(to_integer(unsigned(regBSel))) = "UUUUUUUUUUUUUUUUUUUUUUUUUUUUUUUU") THEN
        outB <= (others => '0');  -- Se o registro for inválido (contém "U"), a saída é zerada
      else
        outB <= registers(to_integer(unsigned(regBSel)));  -- Caso contrário, a saída é o valor do registrador B
      end if;
      -- Write and bypass
      -- Escrita e bypass
      if writeEnable = '1' then
        -- Se o sinal de escrita estiver habilitado (writeEnable = '1'), então o dado de entrada "input" será escrito no registrador selecionado por "writeRegSel"
        registers(to_integer(unsigned(writeRegSel))) <= input;  -- Write
        -- Além disso, é feito o bypass para leitura dos registradores A e B
        if regASel = writeRegSel then  -- Bypass para leitura do registrador A
          outA <= input;  -- O valor de "input" é direcionado para a saída do registrador A
        end if;
        if regBSel = writeRegSel then  -- Bypass para leitura do registrador B
          outB <= input;  -- O valor de "input" é direcionado para a saída do registrador B
        end if;
      end if;
    end if;
  end process;
  -- seleção manual
  -- Saída de um registrador selecionado manualmente com base no valor de "regSelManual"
  outRegManual <= registers(to_integer(unsigned(regSelManual)));
end TypeArchitecture;

// VHDL entity IFID, as the project stores it:
library ieee;
use ieee.std_logic_1164.all;

ENTITY IFID IS
  PORT (
    clk         : IN  std_logic;                    -- Sinal de clock
    pcIn        : IN  std_logic_vector(31 DOWNTO 0); -- PC de entrada (Program Counter)
    pcPl4In     : IN  std_logic_vector(31 DOWNTO 0); -- PC+4 de entrada (PC + 4)
    instIn      : IN  std_logic_vector(31 DOWNTO 0); -- Instrução de entrada
    pcOut       : OUT std_logic_vector(31 DOWNTO 0); -- PC de saída (Program Counter)
    pcPl4Out    : OUT std_logic_vector(31 DOWNTO 0); -- PC+4 de saída (PC + 4)
    instOut     : OUT std_logic_vector(31 DOWNTO 0)  -- Instrução de saída
    );
END IFID;

ARCHITECTURE TypeArchitecture OF IFID IS

SIGNAL IDIF : std_logic_vector(95 DOWNTO 0); -- Registrador interno do estágio IF/ID com 96 bits

BEGIN

	PROCESS (clk)
	BEGIN
		IF (rising_edge(clk)) THEN
			-- No pulso de subida do clock, os dados de entrada são armazenados no registrador IDIF
			IDIF(31 DOWNTO 0) <= instIn;       -- Armazena a instrução
			IDIF(63 DOWNTO 32) <= pcIn;        -- Armazena o PC de entrada
			IDIF(95 DOWNTO 64) <= pcPl4In;     -- Armazena o PC+4 de entrada
		END IF;
		IF (falling_edge(clk)) THEN
			-- No pulso de descida do clock, os dados armazenados no registrador IDIF são disponibilizados nas saídas
			pcOut <= IDIF(63 DOWNTO 32);       -- Fornece o PC de saída
			instOut <= IDIF(31 DOWNTO 0);      -- Fornece a instrução de saída
			pcPl4Out <= IDIF(95 DOWNTO 64);    -- Fornece o PC+4 de saída
		END IF;
	END PROCESS;
	
END TypeArchitecture;

// VHDL entity IDEX, as the project stores it:
library ieee;
use ieee.std_logic_1164.all;

ENTITY IDEX IS
  PORT (
    clk            : IN  std_logic;                     -- Sinal de clock
    pcIn           : IN  std_logic_vector(31 DOWNTO 0); -- PC de entrada (Program Counter)
    read1In        : IN  std_logic_vector(31 DOWNTO 0); -- Registrador de leitura 1 de entrada
    read2In        : IN  std_logic_vector(31 DOWNTO 0); -- Registrador de leitura 2 de entrada
    immGenIn       : IN  std_logic_vector(31 DOWNTO 0); -- Saída do bloco "ImmGen" (gerador de imediatos) de entrada
    aluControlin   : IN  std_logic_vector(3 downto 0);  -- Controle da ALU (Unidade Lógica e Aritmética) de entrada
    wbAddIn        : IN  std_logic_vector(4 downto 0);  -- Endereço do registrador de escrita de volta de entrada
    WBin           : IN  std_logic_vector(2 downto 0);  -- Controle do estágio de escrita de volta (WB) de entrada
    Min            : IN  std_logic_vector(5 downto 0);  -- Controle do estágio de memória (M) de entrada
    EXin           : IN  std_logic_vector(6 downto 0);  -- Controle do estágio de execução (EX) de entrada
    pcPl4In        : IN  std_logic_vector(31 downto 0); -- PC + 4 de entrada
    pcOut          : OUT std_logic_vector(31 DOWNTO 0); -- PC de saída (Program Counter)
    read1Out       : OUT std_logic_vector(31 DOWNTO 0); -- Registrador de leitura 1 de saída
    read2Out       : OUT std_logic_vector(31 DOWNTO 0); -- Registrador de leitura 2 de saída
    immGenOut      : OUT std_logic_vector(31 DOWNTO 0); -- Saída do bloco "ImmGen" (gerador de imediatos) de saída
    aluControlout  : OUT std_logic_vector(3 downto 0);  -- Controle da ALU (Unidade Lógica e Aritmética) de saída
    wbAddOut       : OUT std_logic_vector(4 downto 0);  -- Endereço do registrador de escrita de volta de saída
    WBout          : OUT std_logic_vector(2 downto 0);  -- Controle do estágio de escrita de volta (WB) de saída
    Mout           : OUT std_logic_vector(5 downto 0);  -- Controle do estágio de memória (M) de saída
    EXout          : OUT std_logic_vector(6 downto 0);  -- Controle do estágio de execução (EX) de saída
    pcPl4Out       : OUT std_logic_vector(31 downto 0)  -- PC + 4 de saída
    );
END IDEX;

ARCHITECTURE TypeArchitecture OF IDEX IS

SIGNAL idex_s : std_logic_vector(184 DOWNTO 0); -- Registrador interno do estágio IDEX com 185 bits

BEGIN

	PROCESS (clk)
	BEGIN
		IF (rising_edge(clk)) THEN
			-- No pulso de subida do clock, os dados de entrada são armazenados no registrador idex_s
			idex_s(31 DOWNTO 0)    <= pcIn;
			idex_s(63 DOWNTO 32)   <= read1In;
			idex_s(95 DOWNTO 64)   <= read2In;
			idex_s(127 DOWNTO 96)  <= immGenIn;
			idex_s(131 DOWNTO 128) <= aluControlin;
			idex_s(136 DOWNTO 132) <= wbAddIn;
			idex_s(139 downto 137) <= WBin;
			idex_s(145 downto 140) <= Min;
			idex_s(152 downto 146) <= EXin;
			idex_s(184 downto 153) <= pcPl4In;
		END IF;
		IF (falling_edge(clk)) THEN
			-- No pulso de descida do clock, os dados armazenados no registrador idex_s são disponibilizados nas saídas
			pcOut    <= idex_s(31 DOWNTO 0);
			read1Out <= idex_s(63 DOWNTO 32);
			read2Out <= idex_s(95 DOWNTO 64);
			immGenOut <= idex_s(127 DOWNTO 96);
			aluControlout <= idex_s(131 DOWNTO 128);
			wbAddOut <= idex_s(136 DOWNTO 132);
			WBout <= idex_s(139 downto 137);
			Mout <= idex_s(145 downto 140);
			EXout <= idex_s(152 downto 146);
			pcPl4Out <= idex_s(184 downto 153);
		END IF;
	END PROCESS;
	
END TypeArchitecture;

// VHDL entity EXMEM, as the project stores it:
library ieee;
use ieee.std_logic_1164.all;

ENTITY EXMEM IS
  PORT (
    clk            : IN  std_logic;                     -- Sinal de clock
    sumIn          : IN  std_logic_vector(31 DOWNTO 0); -- Resultado da ALU de entrada
    zeroIn         : IN  std_logic;                     -- Sinal indicando se a saída da ALU é zero de entrada
    aluIn          : IN  std_logic_vector(31 DOWNTO 0); -- Saída da ALU de entrada
    read2In        : IN  std_logic_vector(31 DOWNTO 0); -- Registrador de leitura 2 de entrada
    wbAddIn        : IN  std_logic_vector(4 downto 0);  -- Endereço do registrador de escrita de volta de entrada
    WBin           : IN  std_logic_vector(2 downto 0);  -- Controle do estágio de escrita de volta (WB) de entrada
    Min            : IN  std_logic_vector(5 downto 0);  -- Controle do estágio de memória (M) de entrada
    pcPl4In        : IN  std_logic_vector(31 downto 0); -- PC + 4 de entrada
    pcOut          : OUT std_logic_vector(31 DOWNTO 0); -- PC de saída (Program Counter)
    zeroOut        : OUT std_logic;                     -- Sinal indicando se a saída da ALU é zero de saída
    aluOut         : OUT std_logic_vector(31 DOWNTO 0); -- Saída da ALU de saída
    read2Out       : OUT std_logic_vector(31 DOWNTO 0); -- Registrador de leitura 2 de saída
    wbAddOut       : OUT std_logic_vector(4 downto 0);  -- Endereço do registrador de escrita de volta de saída
    WBout          : OUT std_logic_vector(2 downto 0);  -- Controle do estágio de escrita de volta (WB) de saída
    Mout           : OUT std_logic_vector(5 downto 0);  -- Controle do estágio de memória (M) de saída
    pcPl4Out       : OUT std_logic_vector(31 downto 0)  -- PC + 4 de saída
    );
END EXMEM;

ARCHITECTURE TypeArchitecture OF EXMEM IS

SIGNAL exmem_s : std_logic_vector(142 DOWNTO 0); -- Registrador interno do estágio EXMEM com 143 bits

BEGIN

	PROCESS (clk)
	BEGIN
		IF (rising_edge(clk)) THEN
			-- No pulso de subida do clock, os dados de entrada são armazenados no registrador exmem_s
			exmem_s(31 DOWNTO 0)   <= sumIn;
			exmem_s(32)  <= zeroIn;
			exmem_s(64 DOWNTO 33)  <= aluIn;
			exmem_s(96 DOWNTO 65) <= read2In;
			exmem_s(101 DOWNTO 97) <= wbAddIn;
			exmem_s(104 DOWNTO 102) <= WBin;
			exmem_s(110 DOWNTO 105) <= Min;
			exmem_s(142 downto 111) <= pcPl4In;
		END IF;
		IF (falling_edge(clk)) THEN
			-- No pulso de descida do clock, os dados armazenados no registrador exmem_s são disponibilizados nas saídas
			pcOut    <= exmem_s(31 DOWNTO 0);
			
			if (exmem_s(32) = 'U') then
				zeroOut <= '0';
			else
				zeroOut <= exmem_s(32);
			end if; 

			if (exmem_s(64 DOWNTO 33) = "UUUUUUUUUUUUUUUUUUUUUUUUUUUUUUUU") then
				aluOut <= "00000000000000000000000000000000";
			else
				aluOut <= exmem_s(64 DOWNTO 33);
			end if;
			
			read2Out <= exmem_s(96 DOWNTO 65);
			wbAddOut <= exmem_s(101 DOWNTO 97);
			
			if (exmem_s(110 DOWNTO 105) = "UUUUUU") then
				Mout <= "000000";
			else
				Mout <= exmem_s(110 DOWNTO 105);
			end if;
			
			WBout <= exmem_s(104 DOWNTO 102);

			pcPl4Out <= exmem_s(142 downto 111);
			
			
		END IF;
	END PROCESS;
	
END TypeArchitecture;

// VHDL entity MEMWB, as the project stores it:
library ieee;
use ieee.std_logic_1164.all;

ENTITY MEMWB IS
  PORT (
    clk            : IN  std_logic;                     -- Sinal de clock
    readIn         : IN  std_logic_vector(31 DOWNTO 0); -- Dado lido da memória de entrada
    aluIn          : IN  std_logic_vector(31 DOWNTO 0); -- Saída da ALU de entrada
    wbAddIn        : IN  std_logic_vector(4 downto 0);  -- Endereço do registrador de escrita de volta de entrada
    WBin           : IN  std_logic_vector(2 downto 0);  -- Controle do estágio de escrita de volta (WB) de entrada
    pcPl4In        : IN  std_logic_vector(31 downto 0); -- PC + 4 de entrada
    pcPlIIn        : IN  std_logic_vector(31 downto 0); -- PC + Instrução de 32 bits de entrada
    readOut        : OUT std_logic_vector(31 DOWNTO 0); -- Dado lido da memória de saída
    aluOut         : OUT std_logic_vector(31 DOWNTO 0); -- Saída da ALU de saída
    wbAddOut       : OUT std_logic_vector(4 downto 0);  -- Endereço do registrador de escrita de volta de saída
    WBout          : OUT std_logic_vector(2 downto 0);  -- Controle do estágio de escrita de volta (WB) de saída
    pcPl4Out       : OUT std_logic_vector(31 downto 0); -- PC + 4 de saída
    pcPlIOut       : OUT std_logic_vector(31 downto 0)  -- PC + Instrução de 32 bits de saída
    );
END MEMWB;

ARCHITECTURE TypeArchitecture OF MEMWB IS

SIGNAL memwb_s : std_logic_vector(135 DOWNTO 0); -- Registrador interno do estágio MEMWB com 136 bits

BEGIN

	PROCESS (clk)
	BEGIN
		IF (rising_edge(clk)) THEN
			-- No pulso de subida do clock, os dados de entrada são armazenados no registrador memwb_s
			memwb_s(31 DOWNTO 0)   <= readIn;
			memwb_s(63 DOWNTO 32)  <= aluIn;
			memwb_s(68 DOWNTO 64)  <= wbAddIn;
			memwb_s(71 DOWNTO 69)  <= WBin;
			memwb_s(103 downto 72) <= pcPl4In;
			memwb_s(135 downto 104) <= pcPlIIn;
			
		END IF;
		IF (falling_edge(clk)) THEN
			-- No pulso de descida do clock, os dados armazenados no registrador memwb_s são disponibilizados nas saídas
			readOut    <=  memwb_s(31 DOWNTO 0);
			aluOut  <=  memwb_s(63 DOWNTO 32);
			wbAddOut <= memwb_s(68 DOWNTO 64);
			WBout <= memwb_s(71 DOWNTO 69);
			pcPl4Out <= memwb_s(103 downto 72);
			pcPlIOut <= memwb_s(135 downto 104);
		END IF;
	END PROCESS;
	
END TypeArchitecture;
